// Digital circuit Alu.dig as structural Verilog
module Alu (
  input  [15:0] A,
  input  [15:0] B,
  input  carryIn,
  input  [5:0] AluOp,
  output [15:0] Out,
  output Neg,
  output Zero,
  output CarryOut
);

  wire add_1_c_o, sub_1_c_o;
  wire [15:0] add_1_s, and_2_out, neg_1_out, not_1_out, or_1_out, sub_1_s, xor_1_out;
  wire [15:15] and_1_out;

  and and_1 (and_1_out[15], AluOp[5], carryIn);
  Add #(.Bits(16)) add_1 (.a(A), .b(B), .c_i(and_1_out[15]), .s(add_1_s), .c_o(add_1_c_o));
  Sub #(.Bits(16)) sub_1 (.a(A), .b(B), .c_i(and_1_out[15]), .s(sub_1_s), .c_o(sub_1_c_o));
  assign and_2_out = A & B;  // And and_2, 16 bits wide
  assign or_1_out = A | B;  // Or or_1, 16 bits wide
  assign xor_1_out = A ^ B;  // XOr xor_1, 16 bits wide
  assign not_1_out = ~A;  // Not not_1, 16 bits wide
  Neg #(.Bits(16)) neg_1 (.in(A), .out(neg_1_out));
  Multiplexer #(.Selector_Bits(4), .Bits(16)) multiplexer_1 (
    .sel(AluOp[3:0]), .in_0(B), .in_1(add_1_s), .in_2(sub_1_s), .in_3(and_2_out), .in_4(or_1_out),
    .in_5(xor_1_out), .in_6(not_1_out), .in_7(neg_1_out), .in_8({A[14:0], and_1_out[15]}),
    .in_9({and_1_out[15], A[15:1]}), .in_10({{2{A[15]}}, A[14:1]}), .in_11({A[7:0], A[15:8]}),
    .in_12({A[11:8], A[15:12], A[3:0], A[7:4]}), .in_13(A), .in_14({16{1'b0}}), .in_15({16{1'b0}}),
    .out({Neg, Out[14:0]}));
  Multiplexer #(.Selector_Bits(4)) multiplexer_2 (
    .sel(AluOp[3:0]), .in_0(1'b0), .in_1(add_1_c_o), .in_2(sub_1_c_o), .in_3(1'b0), .in_4(1'b0), .in_5(1'b0),
    .in_6(1'b0), .in_7(1'b0), .in_8(A[15]), .in_9(A[0]), .in_10(A[0]), .in_11(1'b0), .in_12(1'b0),
    .in_13(1'b0), .in_14(1'b0), .in_15(1'b0), .out(CarryOut));
  or_signal #(.applicationType("IVERILOG")) u_or_signal (.D({Neg, Out[14:0]}), .O(Zero));

  assign Out[15] = Neg;

  // Other names for the same wires on the sheet: sel[4:0] = AluOp[4:0]

  // Notes on the sheet:
  //   ALU
  //   logical shift left
  //   logical shift right
  //   arithmetic shift right
  //   swapBytes
  //   swapNibbles
endmodule

/* Code of or_signal:
module or_signal
  (
    input [15:0]D,
    output O
  );

 

  assign O = ~|D;


endmodule
*/
